// Digital circuit ConventionalAlarmClock.dig as structural Verilog
module ConventionalAlarmClock (
  input  CLK,
  input  CLR,
  input  SETUP_TIME,
  input  MIN_ADV,
  input  HR_ADV
);

  BabylonianClock babylonianclock_1 (
    .CLK(CLK), .CLR(CLR), .SETUP(CLR), .MIN_ADV(MIN_ADV), .HR_ADV(HR_ADV));  // open: SECONDS, MINUTES, HOURS
  SevenSegmentDecoder sevensegmentdecoder_1 ();  // open: DATA_IN, DATA_OUT

  assign SETUP_TIME = CLR;
endmodule
