// Digital circuit ControlUnit.dig as structural Verilog
module ControlUnit (
  input  CLK,
  input  RST,
  output END,
  output INIT,
  output EX_OP,
  output SHIFT
);

  wire not_1_out;
  wire [4:0] counter_1_out;

  not not_1 (not_1_out, END);
  Counter #(.Bits(5)) counter_1 (.en(not_1_out), .C(CLK), .clr(RST), .out(counter_1_out));  // open: ovf
  and and_1 (END, counter_1_out[4], counter_1_out[3], counter_1_out[1], counter_1_out[0]);
  nor nor_1 (INIT, counter_1_out[0], counter_1_out[1], counter_1_out[2], counter_1_out[3], counter_1_out[4]);
  and and_2 (EX_OP, ~END, counter_1_out[0], ~INIT);  // And
  D_FF d_ff_1 (.D(EX_OP), .C(CLK), .Q(SHIFT));  // open: nQ

  // Notes on the sheet:
  //   CLK: Hz: 10
endmodule
